# Fritzing sketch Schematic (saved by Fritzing 0.9.3b)
breadboards: 1

parts:
  Part1 = Arduino Uno (Rev3)
  S1 = Momentary Switch [package=ksa_sealed_tac_switch]
  Raspberry_Pi1 = Raspberry Pi 2
  Part4 = Logic Level Converter
  Part2 = Ambient Light Sensor (TEMT6000 Breakout Board)
  R1 = Resistor [tolerance=±5% resistance=220 package="0805 [SMD]"]
  C1 = Capacitor [package=cap-pth-small2]
  Part5 = OLED Monochrome 128x64 1.3 inch [part_number=938]

nets:
  N1: Part1.A0, Part2.S
  N2: Part1.A4/SDA, Part5.MOSI_SDA
  N3: Part1.A5/SCL, Part5.SCLK_SCK
  5V: Part1.AREF, Part1.5V, Part2.VCC, R1.Pin_1, Part5.VIN
  N4: Part1.D0/RX, Part4.RX_HV
  N5: Part1.D1/TX, Part4.TX_HV
  N6: Part1.D2, S1.2, R1.Pin_0, C1.1
  N7: Part1.D4, Part5.RESET
  GND: Part1.GND, S1.3, Part2.GND, C1.2, Part5.GND
  N8: Raspberry_Pi1.GPIO15, Part4.RX_LV
  N9: Raspberry_Pi1.GPIO14, Part4.TX_LV

custom parts:
  OLED Monochrome 128x64 1.3 inch: These displays are small, only about 1.3" diagonal, but very readable due to the high contrast of an OLED display. This display is made of 128x64 individual white OLED pixels, each one is turned on or off by the controller chip. Because the display makes its own light, no backlight is required. This reduces the power required to run the OLED and is why the display has such high contrast; we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
